// Logisim project LogisimCircuit.circ as structural Verilog
module mux2to1_32bit (
  input  [31:0] in0,
  input  [31:0] in1,
  input  s,
  output [31:0] z
);

  wire [31:0] and_1_out, and_2_out, extend32_1_z, not_1_out;

  extend32 extend32_1 (.z(extend32_1_z), .in0(s));
  assign not_1_out = ~extend32_1_z;  // NOT_Gate not_1, 32 bits wide
  assign and_1_out = in0 & not_1_out;  // AND_Gate and_1, 32 bits wide
  assign and_2_out = in1 & extend32_1_z;  // AND_Gate and_2, 32 bits wide
  assign z = and_1_out | and_2_out;  // OR_Gate or_1, 32 bits wide
endmodule

module mux4to2_32bit (
  input  [31:0] in0,
  input  [31:0] in1,
  input  [31:0] in2,
  input  [31:0] in3,
  input  [1:0] s,
  output [31:0] z
);

  wire [31:0] mux2to1_32bit_1_z, mux2to1_32bit_2_z;

  mux2to1_32bit mux2to1_32bit_1 (.z(mux2to1_32bit_1_z), .in1(in1), .in0(in0), .s(s[0]));
  mux2to1_32bit mux2to1_32bit_2 (.z(mux2to1_32bit_2_z), .in1(in3), .in0(in2), .s(s[0]));
  mux2to1_32bit mux2to1_32bit_3 (.z(z), .in1(mux2to1_32bit_2_z), .in0(mux2to1_32bit_1_z), .s(s[1]));
endmodule

module mux8to3_32bit (
  input  [31:0] in0,
  input  [31:0] in1,
  input  [31:0] in2,
  input  [31:0] in3,
  input  [31:0] in4,
  input  [31:0] in5,
  input  [31:0] in6,
  input  [31:0] in7,
  input  [2:0] s,
  output [31:0] z
);

  wire [31:0] mux4to2_32bit_1_z, mux4to2_32bit_2_z;

  mux4to2_32bit mux4to2_32bit_1 (.z(mux4to2_32bit_1_z), .in1(in1), .in2(in2), .in3(in3), .in0(in0), .s(s[1:0]));
  mux4to2_32bit mux4to2_32bit_2 (.z(mux4to2_32bit_2_z), .in1(in5), .in2(in6), .in3(in7), .in0(in4), .s(s[1:0]));
  mux2to1_32bit mux2to1_32bit_1 (.z(z), .in1(mux4to2_32bit_2_z), .in0(mux4to2_32bit_1_z), .s(s[2]));
endmodule

module mux32to5_32bit (
  input  [31:0] in0,
  input  [31:0] in16,
  input  [31:0] in1,
  input  [31:0] in17,
  input  [31:0] in2,
  input  [31:0] in18,
  input  [31:0] in3,
  input  [31:0] in19,
  input  [31:0] in4,
  input  [31:0] in20,
  input  [31:0] in5,
  input  [31:0] in21,
  input  [31:0] in6,
  input  [31:0] in22,
  input  [31:0] in7,
  input  [31:0] in23,
  input  [31:0] in8,
  input  [31:0] in24,
  input  [31:0] in9,
  input  [31:0] in25,
  input  [31:0] in10,
  input  [31:0] in26,
  input  [31:0] in11,
  input  [31:0] in27,
  input  [31:0] in12,
  input  [31:0] in28,
  input  [31:0] in13,
  input  [31:0] in29,
  input  [31:0] in14,
  input  [31:0] in30,
  input  [31:0] in15,
  input  [31:0] in31,
  input  [4:0] s,
  output [31:0] z
);

  wire [31:0] mux4to2_32bit_1_z, mux4to2_32bit_2_z, mux4to2_32bit_3_z, mux4to2_32bit_4_z, mux4to2_32bit_5_z,
       mux4to2_32bit_6_z, mux4to2_32bit_7_z, mux4to2_32bit_8_z, mux4to2_32bit_9_z, mux4to2_32bit_10_z;

  mux4to2_32bit mux4to2_32bit_1 (.z(mux4to2_32bit_1_z), .in1(in1), .in2(in2), .in3(in3), .in0(in0), .s(s[1:0]));
  mux4to2_32bit mux4to2_32bit_2 (.z(mux4to2_32bit_2_z), .in1(in5), .in2(in6), .in3(in7), .in0(in4), .s(s[1:0]));
  mux4to2_32bit mux4to2_32bit_3 (.z(mux4to2_32bit_3_z), .in1(in9), .in2(in10), .in3(in11), .in0(in8), .s(s[1:0]));
  mux4to2_32bit mux4to2_32bit_4 (.z(mux4to2_32bit_4_z), .in1(in13), .in2(in14), .in3(in15), .in0(in12), .s(s[1:0]));
  mux4to2_32bit mux4to2_32bit_5 (
    .z(mux4to2_32bit_5_z), .in1(mux4to2_32bit_2_z), .in2(mux4to2_32bit_3_z), .in3(mux4to2_32bit_4_z),
    .in0(mux4to2_32bit_1_z), .s(s[3:2]));
  mux4to2_32bit mux4to2_32bit_6 (.z(mux4to2_32bit_6_z), .in1(in17), .in2(in18), .in3(in19), .in0(in16), .s(s[1:0]));
  mux4to2_32bit mux4to2_32bit_7 (.z(mux4to2_32bit_7_z), .in1(in21), .in2(in22), .in3(in23), .in0(in20), .s(s[1:0]));
  mux4to2_32bit mux4to2_32bit_8 (.z(mux4to2_32bit_8_z), .in1(in25), .in2(in26), .in3(in27), .in0(in24), .s(s[1:0]));
  mux4to2_32bit mux4to2_32bit_9 (.z(mux4to2_32bit_9_z), .in1(in29), .in2(in30), .in3(in31), .in0(in28), .s(s[1:0]));
  mux4to2_32bit mux4to2_32bit_10 (
    .z(mux4to2_32bit_10_z), .in1(mux4to2_32bit_7_z), .in2(mux4to2_32bit_8_z), .in3(mux4to2_32bit_9_z),
    .in0(mux4to2_32bit_6_z), .s(s[3:2]));
  mux2to1_32bit mux2to1_32bit_1 (.z(z), .in1(mux4to2_32bit_10_z), .in0(mux4to2_32bit_5_z), .s(s[4]));
endmodule

module mux4to2_1bit (
  input  in0,
  input  in1,
  input  in2,
  input  in3,
  input  [1:0] s,
  output z
);

  Multiplexer #(.enable("false"), .select(2)) multiplexer_1 (
    .in0(in0), .in1(in1), .in2(in2), .in3(in3), .out(z), .sel(s));
endmodule

module dec2to4 (
  input  [1:0] in0,
  output out0,
  output out1,
  output out2,
  output out3
);

  wire not_1_out, not_2_out;

  not not_1 (not_1_out, in0[0]);
  not not_2 (not_2_out, in0[1]);
  and and_1 (out0, not_1_out, not_2_out);
  and and_2 (out1, in0[0], not_2_out);
  and and_3 (out2, in0[1], not_1_out);
  and and_4 (out3, in0[0], in0[1]);
endmodule

module dec3to8 (
  input  [2:0] in0,
  output out0,
  output out1,
  output out2,
  output out3,
  output out4,
  output out5,
  output out6,
  output out7
);

  wire not_1_out, not_2_out, not_3_out;

  not not_1 (not_1_out, in0[0]);
  not not_2 (not_2_out, in0[1]);
  not not_3 (not_3_out, in0[2]);
  and and_1 (out0, not_1_out, not_2_out, not_3_out);
  and and_2 (out1, in0[0], not_2_out, not_3_out);
  and and_3 (out2, not_1_out, in0[1], not_3_out);
  and and_4 (out3, in0[0], in0[1], not_3_out);
  and and_5 (out4, not_1_out, not_2_out, in0[2]);
  and and_6 (out5, in0[0], not_2_out, in0[2]);
  and and_7 (out6, not_1_out, in0[1], in0[2]);
  and and_8 (out7, in0[0], in0[1], in0[2]);
endmodule

module dec5to32 (
  input  [4:0] in0,
  output out_2,
  output in8,
  output in16,
  output in24,
  output in1,
  output in9,
  output in17,
  output in25,
  output in2,
  output in10,
  output in18,
  output in26,
  output in3,
  output in11,
  output in19,
  output in27,
  output in4,
  output in12,
  output in20,
  output in28,
  output in5,
  output in13,
  output in21,
  output in29,
  output in6,
  output in14,
  output in22,
  output in30,
  output in7,
  output in15,
  output in23,
  output in31
);

  wire dec2to4_1_out0, dec2to4_1_out1, dec2to4_1_out2, dec2to4_1_out3, dec3to8_1_out0, dec3to8_1_out1,
       dec3to8_1_out2, dec3to8_1_out3, dec3to8_1_out4, dec3to8_1_out5, dec3to8_1_out6, dec3to8_1_out7;

  dec3to8 dec3to8_1 (
    .out2(dec3to8_1_out2), .out3(dec3to8_1_out3), .out4(dec3to8_1_out4), .out5(dec3to8_1_out5),
    .out6(dec3to8_1_out6), .out0(dec3to8_1_out0), .out7(dec3to8_1_out7), .out1(dec3to8_1_out1), .in0(in0[2:0]));
  dec2to4 dec2to4_1 (
    .out2(dec2to4_1_out2), .out3(dec2to4_1_out3), .out0(dec2to4_1_out0), .out1(dec2to4_1_out1), .in0(in0[4:3]));
  and and_1 (out_2, dec3to8_1_out0, dec2to4_1_out0);
  and and_2 (in1, dec3to8_1_out1, dec2to4_1_out0);
  and and_3 (in2, dec3to8_1_out2, dec2to4_1_out0);
  and and_4 (in3, dec3to8_1_out3, dec2to4_1_out0);
  and and_5 (in4, dec3to8_1_out4, dec2to4_1_out0);
  and and_6 (in5, dec3to8_1_out5, dec2to4_1_out0);
  and and_7 (in6, dec3to8_1_out6, dec2to4_1_out0);
  and and_8 (in7, dec3to8_1_out7, dec2to4_1_out0);
  and and_9 (in8, dec3to8_1_out0, dec2to4_1_out1);
  and and_10 (in9, dec3to8_1_out1, dec2to4_1_out1);
  and and_11 (in10, dec3to8_1_out2, dec2to4_1_out1);
  and and_12 (in11, dec3to8_1_out3, dec2to4_1_out1);
  and and_13 (in12, dec3to8_1_out4, dec2to4_1_out1);
  and and_14 (in13, dec3to8_1_out5, dec2to4_1_out1);
  and and_15 (in14, dec3to8_1_out6, dec2to4_1_out1);
  and and_16 (in15, dec3to8_1_out7, dec2to4_1_out1);
  and and_17 (in16, dec3to8_1_out0, dec2to4_1_out2);
  and and_18 (in17, dec3to8_1_out1, dec2to4_1_out2);
  and and_19 (in18, dec3to8_1_out2, dec2to4_1_out2);
  and and_20 (in19, dec3to8_1_out3, dec2to4_1_out2);
  and and_21 (in20, dec3to8_1_out4, dec2to4_1_out2);
  and and_22 (in21, dec3to8_1_out5, dec2to4_1_out2);
  and and_23 (in22, dec3to8_1_out6, dec2to4_1_out2);
  and and_24 (in23, dec3to8_1_out7, dec2to4_1_out2);
  and and_25 (in24, dec3to8_1_out0, dec2to4_1_out3);
  and and_26 (in25, dec3to8_1_out1, dec2to4_1_out3);
  and and_27 (in26, dec3to8_1_out2, dec2to4_1_out3);
  and and_28 (in27, dec3to8_1_out3, dec2to4_1_out3);
  and and_29 (in28, dec3to8_1_out4, dec2to4_1_out3);
  and and_30 (in29, dec3to8_1_out5, dec2to4_1_out3);
  and and_31 (in30, dec3to8_1_out6, dec2to4_1_out3);
  and and_32 (in31, dec3to8_1_out7, dec2to4_1_out3);
endmodule

module reg32 (
  input  [31:0] d,
  input  load,
  input  Clk,
  output [31:0] Q
);

  Register #(.width(32)) register_1 (.D(d), .en(load), .Q(Q), .clk(Clk));  // open: clr
endmodule

module regFile (
  input  [31:0] dData,
  input  w,
  input  [5:0] dAddr,
  input  [5:0] aAddr,
  input  [5:0] bAddr,
  input  Clk,
  output [31:0] aData,
  output [31:0] bData
);
endmodule

module extend16 (
  input  in0,
  output [15:0] z
);


  assign z = {16{in0}};
endmodule

module extend32 (
  input  in0,
  output [31:0] z
);


  assign z = {32{in0}};
endmodule

module fullAdder (
  input  in0,
  input  in1,
  input  cIn,
  output zOut,
  output cOut
);

  wire and_1_out, and_2_out, xor_1_out;

  xor xor_1 (xor_1_out, in1, in0);
  and and_1 (and_1_out, in1, in0);
  xor xor_2 (zOut, xor_1_out, cIn);
  or or_1 (cOut, and_1_out, and_2_out);
  and and_2 (and_2_out, xor_1_out, cIn);
endmodule

module RCA16 (
  input  cIn,
  input  [15:0] in0,
  input  [15:0] in1,
  input  [1:0] s,
  output [15:0] zOut,
  output cOut
);

  wire fulladder_1_cout, fulladder_2_cout, fulladder_3_cout, fulladder_4_cout, fulladder_5_cout,
       fulladder_6_cout, fulladder_7_cout, fulladder_8_cout, fulladder_9_cout, fulladder_10_cout,
       fulladder_11_cout, fulladder_12_cout, fulladder_13_cout, fulladder_14_cout, fulladder_15_cout;
  wire [15:0] and_1_out, and_2_out, extend16_1_z, extend16_2_z, not_1_out, or_1_out;

  extend16 extend16_1 (.z(extend16_1_z), .in0(s[0]));
  extend16 extend16_2 (.z(extend16_2_z), .in0(s[1]));
  assign and_1_out = in1 & extend16_1_z;  // AND_Gate and_1, 16 bits wide
  assign not_1_out = ~in1;  // NOT_Gate not_1, 16 bits wide
  assign and_2_out = not_1_out & extend16_2_z;  // AND_Gate and_2, 16 bits wide
  assign or_1_out = and_1_out | and_2_out;  // OR_Gate or_1, 16 bits wide
  fullAdder fulladder_1 (.cOut(fulladder_1_cout), .zOut(zOut[0]), .in1(or_1_out[0]), .cIn(cIn), .in0(in0[0]));
  fullAdder fulladder_2 (
    .cOut(fulladder_2_cout), .zOut(zOut[1]), .in1(or_1_out[1]), .cIn(fulladder_1_cout), .in0(in0[1]));
  fullAdder fulladder_3 (
    .cOut(fulladder_3_cout), .zOut(zOut[2]), .in1(or_1_out[2]), .cIn(fulladder_2_cout), .in0(in0[2]));
  fullAdder fulladder_4 (
    .cOut(fulladder_4_cout), .zOut(zOut[3]), .in1(or_1_out[3]), .cIn(fulladder_3_cout), .in0(in0[3]));
  fullAdder fulladder_5 (
    .cOut(fulladder_5_cout), .zOut(zOut[4]), .in1(or_1_out[4]), .cIn(fulladder_4_cout), .in0(in0[4]));
  fullAdder fulladder_6 (
    .cOut(fulladder_6_cout), .zOut(zOut[5]), .in1(or_1_out[5]), .cIn(fulladder_5_cout), .in0(in0[5]));
  fullAdder fulladder_7 (
    .cOut(fulladder_7_cout), .zOut(zOut[6]), .in1(or_1_out[6]), .cIn(fulladder_6_cout), .in0(in0[6]));
  fullAdder fulladder_8 (
    .cOut(fulladder_8_cout), .zOut(zOut[7]), .in1(or_1_out[7]), .cIn(fulladder_7_cout), .in0(in0[7]));
  fullAdder fulladder_9 (
    .cOut(fulladder_9_cout), .zOut(zOut[8]), .in1(or_1_out[8]), .cIn(fulladder_8_cout), .in0(in0[8]));
  fullAdder fulladder_10 (
    .cOut(fulladder_10_cout), .zOut(zOut[9]), .in1(or_1_out[9]), .cIn(fulladder_9_cout), .in0(in0[9]));
  fullAdder fulladder_11 (
    .cOut(fulladder_11_cout), .zOut(zOut[10]), .in1(or_1_out[10]), .cIn(fulladder_10_cout), .in0(in0[10]));
  fullAdder fulladder_12 (
    .cOut(fulladder_12_cout), .zOut(zOut[11]), .in1(or_1_out[11]), .cIn(fulladder_11_cout), .in0(in0[11]));
  fullAdder fulladder_13 (
    .cOut(fulladder_13_cout), .zOut(zOut[12]), .in1(or_1_out[12]), .cIn(fulladder_12_cout), .in0(in0[12]));
  fullAdder fulladder_14 (
    .cOut(fulladder_14_cout), .zOut(zOut[13]), .in1(or_1_out[13]), .cIn(fulladder_13_cout), .in0(in0[13]));
  fullAdder fulladder_15 (
    .cOut(fulladder_15_cout), .zOut(zOut[14]), .in1(or_1_out[14]), .cIn(fulladder_14_cout), .in0(in0[14]));
  fullAdder fulladder_16 (.cOut(cOut), .zOut(zOut[15]), .in1(or_1_out[15]), .cIn(fulladder_15_cout), .in0(in0[15]));
endmodule

module RCA32 (
  input  cIn,
  input  [31:0] in0,
  input  [31:0] in1,
  input  [1:0] s,
  output [31:0] zOut,
  output cOut
);

  wire rca16_1_cout;

  RCA16 rca16_1 (.zOut(zOut[15:0]), .cOut(rca16_1_cout), .in0(in0[15:0]), .in1(in1[15:0]), .cIn(cIn), .s(s));
  RCA16 rca16_2 (.zOut(zOut[31:16]), .cOut(cOut), .in0(in0[31:16]), .in1(in1[31:16]), .cIn(rca16_1_cout), .s(s));
endmodule

module logicUnit (
  input  in0,
  input  in1,
  input  [1:0] s,
  output z
);

  wire and_1_out, not_1_out, or_1_out, xor_1_out;

  not not_1 (not_1_out, in0);
  and and_1 (and_1_out, in0, in1);
  or or_1 (or_1_out, in0, in1);
  xor xor_1 (xor_1_out, in0, in1);
  mux4to2_1bit mux4to2_1bit_1 (.z(z), .in2(xor_1_out), .in3(not_1_out), .s(s), .in0(and_1_out), .in1(or_1_out));
endmodule

module FLU16 (
  input  [15:0] in0,
  input  [15:0] in1,
  input  [1:0] s,
  output [15:0] zOut
);

  logicUnit logicunit_1 (.z(zOut[0]), .in0(in0[0]), .in1(in1[0]), .s(s));
  logicUnit logicunit_2 (.z(zOut[1]), .in0(in0[1]), .in1(in1[1]), .s(s));
  logicUnit logicunit_3 (.z(zOut[2]), .in0(in0[2]), .in1(in1[2]), .s(s));
  logicUnit logicunit_4 (.z(zOut[3]), .in0(in0[3]), .in1(in1[3]), .s(s));
  logicUnit logicunit_5 (.z(zOut[4]), .in0(in0[4]), .in1(in1[4]), .s(s));
  logicUnit logicunit_6 (.z(zOut[5]), .in0(in0[5]), .in1(in1[5]), .s(s));
  logicUnit logicunit_7 (.z(zOut[6]), .in0(in0[6]), .in1(in1[6]), .s(s));
  logicUnit logicunit_8 (.z(zOut[7]), .in0(in0[7]), .in1(in1[7]), .s(s));
  logicUnit logicunit_9 (.z(zOut[8]), .in0(in0[8]), .in1(in1[8]), .s(s));
  logicUnit logicunit_10 (.z(zOut[9]), .in0(in0[9]), .in1(in1[9]), .s(s));
  logicUnit logicunit_11 (.z(zOut[10]), .in0(in0[10]), .in1(in1[10]), .s(s));
  logicUnit logicunit_12 (.z(zOut[11]), .in0(in0[11]), .in1(in1[11]), .s(s));
  logicUnit logicunit_13 (.z(zOut[12]), .in0(in0[12]), .in1(in1[12]), .s(s));
  logicUnit logicunit_14 (.z(zOut[13]), .in0(in0[13]), .in1(in1[13]), .s(s));
  logicUnit logicunit_15 (.z(zOut[14]), .in0(in0[14]), .in1(in1[14]), .s(s));
  logicUnit logicunit_16 (.z(zOut[15]), .in0(in0[15]), .in1(in1[15]), .s(s));
endmodule

module FLU32 (
  input  [31:0] in0,
  input  [31:0] in1,
  input  [1:0] s,
  output [31:0] zOut
);

  FLU16 flu16_1 (.zOut(zOut[15:0]), .in1(in1[15:0]), .in0(in0[15:0]), .s(s));
  FLU16 flu16_2 (.zOut(zOut[31:16]), .in1(in1[31:16]), .in0(in0[31:16]), .s(s));
endmodule

module ALU (
  input  [31:0] in0,
  input  [31:0] in1,
  input  [3:0] s,
  output [31:0] zOut,
  output C,
  output V,
  output N
);

  wire and_1_out, and_2_out, not_1_out, not_2_out, not_3_out;
  wire [30:0] rca32_1_zout;
  wire [31:0] flu32_1_zout;

  not not_1 (not_1_out, in0[31]);
  not not_2 (not_2_out, in1[31]);
  RCA32 rca32_1 (.zOut({N, rca32_1_zout}), .cOut(C), .s(s[2:1]), .cIn(s[0]), .in0(in0), .in1(in1));
  FLU32 flu32_1 (.zOut(flu32_1_zout), .s(s[2:1]), .in0(in0), .in1(in1));
  not not_3 (not_3_out, N);
  mux2to1_32bit mux2to1_32bit_1 (.z(zOut), .in1(flu32_1_zout), .in0({N, rca32_1_zout}), .s(s[3]));
  and and_1 (and_1_out, not_3_out, in0[31], in1[31]);
  or or_1 (V, and_1_out, and_2_out);
  and and_2 (and_2_out, N, not_1_out, not_2_out);
endmodule

module zDetect (
  input  [31:0] in0,
  output z
);

  wire or_1_out;

  or or_1 (or_1_out, in0[0], in0[1], in0[2], in0[3], in0[4], in0[5], in0[6], in0[7], in0[8], in0[9], in0[10], in0[11], in0[12], in0[13], in0[14], in0[15], in0[16], in0[17], in0[18], in0[19], in0[20], in0[21], in0[22], in0[23], in0[24], in0[25], in0[26], in0[27], in0[28], in0[29], in0[30], in0[31]);
  not not_1 (z, or_1_out);
endmodule

module shifter (
  input  [31:0] in0,
  input  [1:0] s,
  output [31:0] z
);

  mux4to2_32bit mux4to2_32bit_1 (
    .z(z), .in1({in0[30:0], 1'b0}), .in2({1'b0, in0[31:1]}), .in0(in0), .s(s));  // open: in3
endmodule

module funcUnit (
  input  [31:0] in0,
  input  [31:0] in1,
  input  [4:0] s,
  output [31:0] zOut,
  output C,
  output V,
  output N,
  output Z
);

  wire [31:0] alu_1_zout, shifter_1_z;

  ALU alu_1 (.zOut(alu_1_zout), .C(C), .V(V), .N(N), .s(s[3:0]), .in0(in0), .in1(in1));
  shifter shifter_1 (.z(shifter_1_z), .in0(in1), .s(s[3:2]));
  mux2to1_32bit mux2to1_32bit_1 (.z(zOut), .in1(shifter_1_z), .in0(alu_1_zout), .s(s[4]));
  zDetect zdetect_1 (.z(Z), .in0(alu_1_zout));
endmodule

module dataPath (
  input  w,
  input  [5:0] dAddr,
  input  [5:0] aAddr,
  input  [5:0] bAddr,
  input  MBsel,
  input  [31:0] dData,
  input  MDsel,
  input  [4:0] opIn,
  output [31:0] aBus,
  output [31:0] bBus,
  output [31:0] dBus,
  output Vout,
  output Cout,
  output Nout,
  output Zout
);

  wire clock_1_out;
  wire [31:0] funcunit_1_zout, regfile_1_bdata;

  Clock clock_1 (.out(clock_1_out));
  regFile regfile_1 (
    .dData(dBus), .w(w), .dAddr(dAddr), .aAddr(aAddr), .bAddr(bAddr), .Clk(clock_1_out), .aData(aBus),
    .bData(regfile_1_bdata));
  funcUnit funcunit_1 (
    .zOut(funcunit_1_zout), .C(Cout), .V(Vout), .N(Nout), .Z(Zout), .s(opIn), .in0(aBus), .in1(bBus));
  mux2to1_32bit mux2to1_32bit_1 (.z(bBus), .in1({32{1'b0}}), .in0(regfile_1_bdata), .s(MBsel));
  mux2to1_32bit mux2to1_32bit_2 (.z(dBus), .in1(dData), .in0(funcunit_1_zout), .s(MDsel));
endmodule
